# Fritzing sketch BoxSack (saved by Fritzing 0.9.3b)
breadboards: 1

parts:
  Bauteil1 = ws2812b [package="smd 2812b"]
  Bauteil2 = Arduino Nano No Internal
  GY1 = MPU-6050 Board GY-521 [form="♀ (female)" package=THT]

nets:
  VDD: Bauteil1.VDD, Bauteil2.5V, GY1.pin1
  VSS: Bauteil1.VSS, Bauteil2.GND, GY1.pin2
  N1: Bauteil1.DIN, Bauteil2.D6
  N2: Bauteil2.A5, GY1.pin3
  N3: Bauteil2.A4, GY1.pin4

custom parts:
  Arduino Nano No Internal: The Arduino Nano is a small, complete, and breadboard-friendly board based on the ATmega328 (Arduino Nano 3.0) or ATmega168 (Arduino Nano 2.x). It has more or less the same functionality of the Arduino Duemilanove, but in a different package. It lacks only a DC power jack, and works with a Mini-B USB cable instead of a standard one. The Nano was designed and is being produced by Gravitech.
  MPU-6050 Board GY-521: Acelerometro y Giroscopio MPU-6050 Board GY-521
